// Logisim project control.circ as structural Verilog: 1 circuit, main circuit Control
module Control (
  input  done,
  input  start,
  input  clock,
  output count,
  output lm,
  output lp,
  output sm
);

  wire and_1_out, and_2_out, and_5_out;
  wire [2:0] N0_out, register_1_q;

  Register #(.width(3)) register_1 (.D(N0_out), .Q(register_1_q), .clk(clock));  // open: en, clr
  // Probe on register_1_q
  and and_1 (and_1_out, ~register_1_q[0], ~register_1_q[1], ~register_1_q[2], start);  // AND_Gate
  or N0 (N0_out[0], and_1_out, and_2_out);
  and and_2 (and_2_out, ~register_1_q[2], register_1_q[1], ~register_1_q[0]);  // AND_Gate
  and and_3 (sm, ~register_1_q[2], ~register_1_q[1], register_1_q[0]);  // AND_Gate
  and and_4 (lp, ~register_1_q[2], register_1_q[1], ~register_1_q[0]);  // AND_Gate
  or N1 (N0_out[1], sm, lp, and_5_out);
  and and_5 (and_5_out, ~register_1_q[2], register_1_q[1], register_1_q[0], ~done);  // AND_Gate
  or or_1 (lm, lp, sm);
  and N3 (N0_out[2], ~register_1_q[2], register_1_q[1], register_1_q[1], done);  // AND_Gate
  and and_6 (count, ~register_1_q[2], register_1_q[1], register_1_q[0]);  // AND_Gate
endmodule
