// Logisim project datapath.circ as structural Verilog: 8 circuits, main circuit Data path
// 0x21
module Data_path (
  input  multipliar_signal,
  input  product_signal,
  input  [31:0] multiplicant,
  input  [31:0] multipliar,
  input  count_signal,
  input  start_multipliar,
  input  clock_signal,
  output [31:0] product_reg_output,
  output [31:0] multipliar_reg_output,
  output stop
);

  wire [5:0] counter_1_q;
  wire [31:0] multiplexer_1_out, n32_bit_alu_1_multipliar_alu_result, n32_bit_alu_1_product_alu_result;

  _32_bit_ALU u_32_bit_alu_1 (
    .product(product_reg_output), .multiplicant(multiplicant),
    .Product_ALU_Result(n32_bit_alu_1_product_alu_result), .multipliar(multipliar_reg_output),
    .Multipliar_ALU_Result(n32_bit_alu_1_multipliar_alu_result), .ALU_SGN(multipliar_reg_output[0]));
  Multiplexer #(.width(32)) multiplexer_1 (
    .in0(n32_bit_alu_1_multipliar_alu_result), .in1(multipliar), .out(multiplexer_1_out),
    .sel(start_multipliar));  // open: en
  Register #(.width(32)) u_multipliar (
    .D(multiplexer_1_out), .en(multipliar_signal), .Q(multipliar_reg_output), .clk(clock_signal));  // open: clr
  Register #(.width(32)) product (
    .D(n32_bit_alu_1_product_alu_result), .en(product_signal), .Q(product_reg_output), .clk(clock_signal));  // open: clr
  Counter #(.width(6), .max('h1f), .ongoal("stay")) counter_1 (
    .count(count_signal), .Q(counter_1_q), .clk(clock_signal));  // open: load, D, carry, clr
  // Probe on counter_1_q
  comparator comparator_1 (.a(counter_1_q), .b(6'b011111), .out_3(stop));
endmodule

module _32_bit_ALU (
  input  [31:0] product,
  input  [31:0] multiplicant,
  input  [31:0] multipliar,
  input  ALU_SGN,
  output [31:0] Product_ALU_Result,
  output [31:0] Multipliar_ALU_Result
);

  wire [31:0] adder_1_out, multiplexer_1_out;

  Adder #(.width(32)) adder_1 (.a(product), .b(multiplicant), .out(adder_1_out));  // open: cin, cout
  Multiplexer #(.width(32)) multiplexer_1 (
    .in0(product), .in1(adder_1_out), .out(multiplexer_1_out), .sel(ALU_SGN));  // open: en
  Shifter shifter_1 (
    .Product(multiplexer_1_out), .Multipliar(multipliar), .Shifted_Product(Product_ALU_Result),
    .Shifted_Multipliar(Multipliar_ALU_Result));
endmodule

module Shifter (
  input  [31:0] Product,
  input  [31:0] Multipliar,
  output [31:0] Shifted_Product,
  output [31:0] Shifted_Multipliar
);

  wire [31:0] shifter_2_out;

  Shifter_part #(.width(32), .shift("lr")) shifter_1 (.in(Product), .\dist (5'b00001), .out(Shifted_Product));
  Shifter_part #(.width(32), .shift("lr")) shifter_2 (.in(Multipliar), .\dist (5'b00001), .out(shifter_2_out));
  assign Shifted_Multipliar = {Product[0], {31{1'b0}}} | shifter_2_out;  // OR_Gate or_1, 32 bits wide
endmodule

module comparator (
  input  [5:0] a,
  input  [5:0] b,
  output out_3
);

  wire xnor_1_out, xnor_2_out, xnor_3_out, xnor_4_out, xnor_5_out, xnor_6_out;

  xnor xnor_1 (xnor_1_out, a[0], b[0]);
  xnor xnor_2 (xnor_2_out, a[1], b[1]);
  xnor xnor_3 (xnor_3_out, a[2], b[2]);
  xnor xnor_4 (xnor_4_out, a[3], b[3]);
  xnor xnor_5 (xnor_5_out, a[4], b[4]);
  xnor xnor_6 (xnor_6_out, a[5], b[5]);
  and and_1 (out_3, xnor_3_out, xnor_1_out, xnor_2_out, xnor_4_out, xnor_5_out, xnor_6_out);
endmodule

module test_shifter (
  input  [31:0] in_1,
  input  [31:0] in_2,
  output [31:0] out_3,
  output [31:0] out_4
);

  Shifter shifter_1 (.Product(in_1), .Multipliar(in_2), .Shifted_Product(out_3), .Shifted_Multipliar(out_4));
  // Probe on out_3
  // Probe on out_4
endmodule

module test_comperator (
  input  [4:0] in_1,
  input  [4:0] in_2,
  output out_3
);

  // comparator comparator_1: pin names not known; wires that end beside it: in_1, in_2, out_3
endmodule

module test_ALU (
  input  [31:0] product,
  input  [31:0] multipliar,
  input  in_3,
  input  [31:0] multiplicant,
  output [31:0] out_5,
  output [31:0] out_6
);

  _32_bit_ALU u_32_bit_alu_1 (
    .product(product), .multiplicant(multiplicant), .Product_ALU_Result(out_5), .multipliar(multipliar),
    .Multipliar_ALU_Result(out_6), .ALU_SGN(in_3));
endmodule

module test_datapath (
  input  in_1,
  input  [31:0] multipliar,
  input  [31:0] multiplicant,
  input  in_4,
  output [31:0] product,
  output [31:0] multipliar_2,
  output out_7
);

  wire button_1_out;

  // Probe on multipliar
  // Probe on multiplicant
  Button button_1 (.out(button_1_out));
  // Data_path data_path_1: pin names not known; wires that end beside it: multipliar, multiplicant, in_4, button_1_out, multipliar_2, out_7
  // Probe on product
  // Probe on multipliar_2
endmodule
