// Logisim project mult32.circ as structural Verilog: 1 circuit, main circuit main
module main (
  input  [31:0] Multipliar,
  input  [31:0] Multiplicant,
  output [31:0] out_3,
  output [31:0] out_4
);

  wire clock_1_out, control_1_count, control_1_lm, control_1_lp, control_1_sm, data_path_1_stop, Start_out;

  Button Start (.out(Start_out));
  Clock clock_1 (.out(clock_1_out));
  // Probe on Multipliar
  // Probe on Multiplicant
  Control control_1 (
    .lm(control_1_lm), .lp(control_1_lp), .sm(control_1_sm), .clock(clock_1_out), .start(Start_out),
    .done(data_path_1_stop), .count(control_1_count));
  Data_path data_path_1 (
    .multipliar(Multipliar), .multiplicant(Multiplicant), .product_reg_output(out_3),
    .multipliar_reg_output(out_4), .multipliar_signal(control_1_lm), .product_signal(control_1_lp),
    .start_multipliar(control_1_sm), .clock_signal(clock_1_out), .stop(data_path_1_stop),
    .count_signal(control_1_count));
  // Probe on out_3
  // Probe on out_4
endmodule
